// Digital circuit 4bitALU.dig as structural Verilog
module _4bitALU (
  input  [3:0] A,
  input  [3:0] B,
  input  OP,
  output [3:0] O,
  output Co
);

  wire [3:0] _1mux_1_o, _4bitnegator_1_o;

  _4bitNegator _4bitnegator_1 (.I(B), .O(_4bitnegator_1_o));
  _1mux _1mux_1 (.A(B), .B(_4bitnegator_1_o), .Sel(OP), .O(_1mux_1_o));
  _4bitAdder _4bitadder_1 (.A(A), .B(_1mux_1_o), .S(O), .C(Co));
endmodule
