// Digital circuit 4bitCPU.dig as structural Verilog
module _4bitCPU (
  input  [3:0] A,
  input  [3:0] B,
  input  CP,
  input  [1:0] OP,
  output Co,
  output [3:0] O
);

  wire _4bitequals_1_eq, nand_1_out, nandand_1_c;
  wire [3:0] _1mux_1_o, _1mux_2_o, _4bitadder_1_s, _4bitregister_1_q, _4bitregister_2_q, _4bitregister_3_q,
       _4bitregister_4_q;

  _4bitRegister _4bitregister_1 (.D(A), .CP(nandand_1_c), .Q(_4bitregister_1_q));
  _4bitRegister _4bitregister_2 (.D(B), .CP(nandand_1_c), .Q(_4bitregister_2_q));
  _1mux _1mux_1 (.A(4'b1111), .B(_4bitadder_1_s), .Sel(OP[1]), .O(_1mux_1_o));
  _4bitRegister _4bitregister_3 (.D(_1mux_1_o), .CP(nandand_1_c), .Q(_4bitregister_3_q));
  _4bitEquals _4bitequals_1 (.A(_4bitregister_2_q), .B(_4bitadder_1_s), .eq(_4bitequals_1_eq));
  nand nand_1 (nand_1_out, OP[1], _4bitequals_1_eq);
  _4bitAdder _4bitadder_1 (.A(_4bitregister_3_q), .B(4'b0001), .S(_4bitadder_1_s));  // open: C
  nandAND nandand_1 (.A(CP), .B(nand_1_out), .C(nandand_1_c));
  _1mux _1mux_2 (.A(_4bitregister_2_q), .B(_4bitregister_4_q), .Sel(OP[1]), .O(_1mux_2_o));
  _4bitALU _4bitalu_1 (.A(_4bitregister_1_q), .B(_1mux_2_o), .OP(OP[0]), .O(O), .Co(Co));
  _4bitRegister _4bitregister_4 (.D(O), .CP(nandand_1_c), .Q(_4bitregister_4_q));
endmodule
